# Fritzing sketch Circuit Diagram (saved by Fritzing 0.9.3b)
breadboards: 1

parts:
  U1 = ESP8266 NodeMCU LoLin module
  U2 = ESP8266 NodeMCU LoLin module
  KY-1 = Keyes Relay [package=THT]
  LED1 = RGB LED - (4 legs) [package="5 mm [THT]"]
  LED2 = RGB LED - (4 legs) [package="5 mm [THT]"]
  LED4 = LEDs [package=led10mm]
  LED5 = LEDs [package=led10mm]
  LED6 = LEDs [package=led10mm]
  U4 = LIPO-110mAh [package=lipo-110]
  M1 = DC Motor
  LED7 = RGB LED - (4 legs) [package="5 mm [THT]"]

nets:
  N1: U1.D0, KY-1.signal
  N2: U1.D1, LED7.blue_cathode
  N3: U1.D2, LED7.common_anode
  N4: U1.D3, LED7.red_cathode
  N5: U1.D4, LED4.A
  N6: U1.3V3, KY-1.power, LED2.green_cathode, LED7.green_cathode
  N7: U1.GND, KY-1.ground, LED4.C, LED5.C
  N8: U1.D5, LED2.blue_cathode
  N9: U1.D6, LED2.common_anode
  N10: U1.D7, LED2.red_cathode
  N11: U1.D8, LED5.A
  N12: U2.D0, LED6.A
  N13: U2.D1, LED1.blue_cathode
  N14: U2.D2, LED1.common_anode
  N15: U2.D3, LED1.red_cathode
  N16: U2.3V3, LED1.green_cathode
  N17: U2.GND, LED6.C
  N18: KY-1.C, M1.pin_2
  N19: KY-1.NO, U4.-
  N20: U4.+, M1.pin_1

custom parts:
  ESP8266 NodeMCU LoLin module: ESP8266 based NodeMCU
  Keyes Relay: The Keyes 5V relay module is suitable for SCM development, home appliance control. It uses a 5V~12V TIL control signal which can control DC / AC signal.
